# Fritzing sketch Esp32_devkit_design (saved by Fritzing 0.9.9b)

parts:
  S1 = Pushbutton [package="[THT]"]
  R1 = Resistor [tolerance=±5% resistance=10k package=THT]
  LED1 = RGB LED (com. cathode, rgb) [package="5 mm [THT]"]
  R2 = Resistor [tolerance=±5% resistance=680 package=THT]
  R3 = Resistor [tolerance=±5% resistance=680 package=THT]
  R4 = Resistor [tolerance=±5% resistance=680 package=THT]
  RHT1 = Humidity and Temperature Sensor RHT03
  R5 = Resistor [tolerance=±5% resistance=3.3k package=THT]
  C2 = Ceramic Capacitor [capacitance=100nF voltage=35V package="100 mil [THT, multilayer]"]
  R7 = Trimmer Potentiometer [maximum_resistance=10kΩ package=THT]
  U1 = Sharp PC817 [package=THT]
  LED2 = LED - 5mm [color="Red (633nm)" package="5 mm [THT]"]
  R8 = Resistor [tolerance=±5% resistance=10k package=THT]
  J1 = single row smd female pin header, 2 pins [form="♀ (female)"]
  M1 = DOIT Esp32 DevKit v1 (30 pins long, 11 pins width) [part_number=ESP32S-PIN30]

nets:
  N1: S1.Pin_1, S1.Pin_2, R1.Pin_1, M1.D34
  VCC: S1.Pin_4, RHT1.Vcc, C2.1, R8.Pin_1, M1.3V3
  N2: R1.Pin_0, LED1.common_cathode, RHT1.GND_2, C2.0, U1.Pin_3, M1.GND
  N3: LED1.red_anode, R4.Pin_1
  N4: LED1.green_anode, R3.Pin_1
  N5: LED1.blue_anode, R2.Pin_1
  N6: R2.Pin_0, M1.D26
  N7: R3.Pin_0, M1.D27
  N8: R4.Pin_0, M1.D14
  N9: RHT1.Data-signal, R5.Pin_1
  N10: R5.Pin_0, M1.D4
  N11: R7.leg1, J1.pin2
  N12: R7.wiper, U1.Pin_2
  N13: U1.Pin_1, LED2.cathode
  N14: U1.Pin_4, R8.Pin_0, M1.D18
  N15: LED2.anode, J1.pin1

custom parts:
  DOIT Esp32 DevKit v1 (30 pins long, 11 pins width): The DOIT Esp32 DevKit v1 is one of the development board created by DOIT to evaluate the ESP-WROOM-32 module. It is based on the ESP32 microcontroller that boasts Wifi, Bluetooth, Ethernet and Low Power support all in a single chip. (vanepp) made breadboard work, adjusted pin numbering and labels and reduced size of schematic and cleaned up pcb. This chip is 30pins long (2 x15) and 11 pins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
